// Logisim project zadanie36.circ as structural Verilog: 1 circuit, main circuit main
module main (
  input  A,
  input  B,
  input  C,
  input  D,
  output Y,
  output Z,
  output Y_DNF,
  output Z_DNF,
  output Y_KNF,
  output Z_KNF
);

  wire B_C_D_out, B_nC_out, n_A_B_out, n_B_D_out, n_C_nD_out, nB_C_out, nB_nC_D_out, not_1_out, not_2_out,
       not_3_out;

  not not_1 (not_1_out, D);
  not not_2 (not_2_out, B);
  not not_3 (not_3_out, C);
  nor n_A_B (n_A_B_out, B, A);
  nor n_C_nD (n_C_nD_out, not_1_out, C);
  nand n_B_D (n_B_D_out, D, B);
  or A_B_C_nD (Y_DNF, A, B, C, not_1_out);
  and nB_nC_D (nB_nC_D_out, not_2_out, not_3_out, D);
  and B_C_D (B_C_D_out, B, C, D);
  or B_nC (B_nC_out, B, not_3_out);
  or nB_C (nB_C_out, not_2_out, C);
  nand n_n_A_B__n_C_nD (Y, n_A_B_out, n_C_nD_out);
  xnor n_C_nD__n_B_D__n_n_C_nD___n_n_B_D (Z, n_C_nD_out, n_B_D_out);
  or nB_nC_D_B_C_D (Z_DNF, nB_nC_D_out, B_C_D_out);
  and D__B_nC___nB_C (Z_KNF, B_nC_out, D, nB_C_out);

  assign Y_KNF = Y_DNF;

  // Notes on the sheet:
  //   NOT D
  //   NOT B
  //   NOT C
  //   Zadanie
  //   DNF
  //   KNF
endmodule
