// Logisim project 2_zad.circ as structural Verilog: 1 circuit, main circuit main
module main (
  input  a,
  input  b,
  input  c,
  input  d,
  output A_D,
  output B_D,
  output C_D,
  output D_D,
  output A_K,
  output B_K,
  output C_K,
  output D_K
);

  nand nc (C_D, c, c);
  nand nd (D_D, d, d);

  assign A_D = a;
  assign A_K = a;
  assign B_D = b;
  assign B_K = b;
  assign C_K = C_D;
  assign D_K = D_D;
endmodule
