// Logisim project zadanie36.circ as structural Verilog: 1 circuit, main circuit main
module main (
  input  A,
  input  B,
  input  C,
  input  D,
  output x,
  output y
);

  wire nand_1_out, nor_1_out, nor_2_out, not_1_out;

  not not_1 (not_1_out, D);
  nor nor_1 (nor_1_out, B, A);
  nor nor_2 (nor_2_out, not_1_out, C);
  nand nand_1 (nand_1_out, D, B);
  nand nand_2 (x, nor_1_out, nor_2_out);
  xnor xnor_1 (y, nor_2_out, nand_1_out);
endmodule
